// Logisim project 7400-series-rev1.circ as structural Verilog: 25 circuits, main circuit main
module main (
);

  _74xx00 u_74xx00_1 ();  // open: _1A_1, _1B_2, _2A_4, _2B_5, _3A_9, _3B_10, _4A_12, _4B_13, Vcc_14, Gnd_7, _1Y_3, _2Y_6, _3Y_8, _4Y_11, Power_Test_imaginary
  _74xx20 u_74xx20_1 ();  // open: _1A_1, _1B_2, _1C_4, _1D_5, _2A_9, _2B_10, _2C_12, _2D_13, Vcc_14, Gnd_7, _1Y_6, _2Y_8, Power_Test_imaginary
  _74xx42 u_74xx42_1 ();  // open: S0_15, S1_14, S2_13, S3_12, Vcc_14, Gnd_7, Y0_1, Y1_2, Y2_3, Y3_4, Y4_5, Y5_6, Y6_7, Y7_9, Y8_10, Y9_11, Power_Test_imaginary
  _74XX02 u_74xx02_1 ();  // open: _1A_1, _1B_2, _2A_4, _2B_5, _3A_8, _3B_9, _4A_11, _4B_12, Vcc_14, Gnd_7, _1Y_3, _2Y_6, _3Y_10, _4Y_13, Power_Test_imaginary
  _74xx21 u_74xx21_1 ();  // open: _1A_1, _1B_2, _1C_4, _1D_5, _2A_9, _2B_10, _2C_12, _2D_13, Vcc_14, Gnd_7, _1Y_6, _2Y_8, Power_Test_imaginary
  _74xx55 u_74xx55_1 ();  // open: A__1, B__2, C__3, D__4, H__13, G__12, F__11, E__10, Vcc_14, Gnd_7, Y__8, Power_Test_imaginary
  _74xx04 u_74xx04_1 ();  // open: _1A_1, _2A_3, _3A_5, _4A_9, _5A_11, _6A_13, Vcc_14, Gnd_7, _1Y_2, _2Y_4, _3Y_6, _4Y_8, _5Y_10, _6Y_12, Power_Test_imaginary
  _74xx24 u_74xx24_1 ();  // open: _1A_1, _1B_2, _2A_4, _2B_5, _3A_9, _3B_10, _4A_12, _4B_13, Vcc_14, Gnd_7, _1Y_3, _2Y_6, _3Y_8, _4Y_11, Power_Test_imaginary
  _74xx260 u_74xx260_1 ();  // open: _1A__1, _1B__2, _1C__4, _1D__5, _1E__3, _2A__9, _2B__10, _2C__12, _2D__13, _2E__11, Vcc_14, Gnd_7, _1Y__6, _2Y__8, Power_Test_imaginary
  _74xx08 u_74xx08_1 ();  // open: _1A_1, _1B_2, _2A_4, _2B_5, _3A_9, _3B_10, _4A_12, _4B_13, Vcc_14, Gnd_7, _1Y_3, _2Y_6, _3Y_8, _4Y_11, Power_Test_imaginary
  _74xx10 u_74xx10_1 ();  // open: _1A_1, _1B_2, _1C_13, _2A_3, _2B_4, _2C_5, _3A_9, _3B_10, _3C_11, Vcc_14, Gnd_7, _1Y_12, _2Y_6, _3Y_8, Power_Test_imaginary
  _74xx27 u_74xx27_1 ();  // open: _1A_1, _1B_2, _1C_13, _2A_3, _2B_4, _2C_5, _3A_9, _3B_10, _3C_11, Vcc_14, Gnd_7, _1Y_12, _2Y_6, _3Y_8, Power_Test_imaginary
  _74xx25 u_74xx25_1 ();  // open: _1A_1, _1B_2, _1C__4, _1D__5, _1G__3, _2A_9, _2B_10, _2C__12, _2D__13, _2G__11, Vcc_14, Gnd_7, _1Y_3, _2Y_8, Power_Test_imaginary
  _74xx590 u_74xx590_1 ();  // open: CPR_13, CPC_11, nCE_12, nMRC_10, nOE_14, Q0_15, Q1_1, Q2_2, Q3_3, Q4_4, Q5_5, Q6_6, Q7_7, nRCO_9
  _74xx11 u_74xx11_1 ();  // open: _1A_1, _1B_2, _1C_13, _2A_3, _2B_4, _2C_5, _3A_9, _3B_10, _3C_11, Vcc_14, Gnd_7, _1Y_12, _2Y_6, _3Y_8, Power_Test_imaginary
  _74xx28 u_74xx28_1 ();  // open: _1A_2, _1B_3, _2A_5, _2B_6, _3A_9, _3B_9, _4A_11, _4B_12, Vcc_14, Gnd_7, _1Y_1, _2Y_4, _3Y_10, _4Y_13, Power_Test_imaginary
  _74xx13 u_74xx13_1 ();  // open: _1A_1, _1B_2, _1C_4, _1D_5, _2A_9, _2B_10, _2C_12, _2D_13, Vcc_14, Gnd_7, _1Y_6, _2Y_8, Power_Test_imaginary
  _74xx30 u_74xx30_1 ();  // open: A_1, B_2, C_3, D_4, E_5, F_6, G_11, H_12, Vcc_14, Gnd_7, nY_8, Power_Test_imaginary
  _74xx14 u_74xx14_1 ();  // open: _1A_1, _2A_3, _3A_5, _4A_9, _5A_11, _6A_13, Vcc_14, Gnd_7, _1Y_2, _2Y_4, _3Y_6, _4Y_8, _5Y_10, _6Y_12, Power_Test_imaginary
  _74xx18 u_74xx18_1 ();  // open: _1A_1, _1B_2, _1C_4, _1D_5, _2A_9, _2B_10, _2C_12, _2D_13, Vcc_14, Gnd_7, _1Y_6, _2Y_8, Power_Test_imaginary
  _74xx37 u_74xx37_1 ();  // open: _1A_1, _1B_2, _2A_4, _2B_5, _3A_9, _3B_10, _4A_12, _4B_13, Vcc_14, Gnd_7, _1Y_3, _2Y_6, _3Y_8, _4Y_11, Power_Test_imaginary
  _74xx32 u_74xx32_1 ();  // open: _1A_1, _1B_2, _2A_4, _2B_5, _3A_9, _3B_10, _4A_12, _4B_13, Vcc_14, Gnd_7, _1Y_3, _2Y_6, _3Y_8, _4Y_11, Power_Test_imaginary
  _74xx19 u_74xx19_1 ();  // open: _1A_1, _2A_3, _3A_5, _4A_9, _5A_11, _6A_13, Vcc_14, Gnd_7, _1Y_2, _2Y_4, _3Y_6, _4Y_8, _5Y_10, _6Y_12, Power_Test_imaginary
  _74xx40 u_74xx40_1 ();  // open: _1A_1, _1B_2, _1C_4, _1D_5, _2A_9, _2B_10, _2C_12, _2D_13, Vcc_14, Gnd_7, _1Y_6, _2Y_8, Power_Test_imaginary

  // Notes on the sheet:
  //   Copyright 2005 Technological Services Company
  //   74xx00
  //   74xx20
  //   74xx42
  //   These circuits are distributed under the same GPL terms as Logisim.
  //   You must load Logisim's Built-in Libraries for these to work.
  //   Point to the pins to see a description.  Some show power and imaginary pins. See examples below.
  //   (Terminal Numbers) are for PDIP packages unless stated otherwise.
  //   No open collector type chips are included.
  //   74xx04
  //   74xx02
  //   74xx21
  //   74xx24
  //   74xx55
  //   74xx260
  //   74xx08
  //   74xx25
  //   74xx590
  //   74xx10
  //   74xx27
  //   7xx11
  //   74xx13
  //   74xx28
  //   74xx30
  //   74xx14
  //   74xx32
  //   RELEASE NOTES:
  //   Rev.1: 12/12//05,  Initial Release, 00-50 plus others
  //   Acknowledgements:
  //   Special Thanks to Carl Burch for creating Logisim.
  //   Matthew Sheffield built most of the basic gate type chips.
  //   W. L. "Bud" Nail, served as mentor, and technical advisior.
  //   74xx18
  //   74xx37
  //   74xx19
  //   74xx40
endmodule

module _74xx00 (
  input  _1A_1,
  input  _1B_2,
  input  _2A_4,
  input  _2B_5,
  input  _3A_9,
  input  _3B_10,
  input  _4A_12,
  input  _4B_13,
  input  Vcc_14,
  input  Gnd_7,
  output _1Y_3,
  output _2Y_6,
  output _3Y_8,
  output _4Y_11,
  output Power_Test_imaginary
);

  wire not_1_out;

  not not_1 (not_1_out, Gnd_7);
  nand nand_1 (_1Y_3, _1A_1, _1B_2, _1B_2);
  nand nand_2 (_2Y_6, _2A_4, _2B_5, _2B_5);
  nand nand_3 (_3Y_8, _3A_9, _3B_10, _3B_10);
  nand nand_4 (_4Y_11, _4A_12, _4B_13, _4B_13);
  and and_1 (Power_Test_imaginary, Vcc_14, Vcc_14, not_1_out);

  // Notes on the sheet:
  //   _1A_1: pull=up
  //   _2A_4: pull=up
  //   _1B_2: pull=up
  //   Vcc_14: pull=down
  //   _2B_5: pull=up
  //   _3A_9: pull=up
  //   _3B_10: pull=up
  //   _4B_13: pull=up
  //   _4A_12: pull=up
  //   74xx00 Quad 2-input NAND Gate
  //   Copyright 2005 Technological Services Company
endmodule

module _74XX02 (
  input  _1A_1,
  input  _1B_2,
  input  _2A_4,
  input  _2B_5,
  input  _3A_8,
  input  _3B_9,
  input  _4A_11,
  input  _4B_12,
  input  Vcc_14,
  input  Gnd_7,
  output _1Y_3,
  output _2Y_6,
  output _3Y_10,
  output _4Y_13,
  output Power_Test_imaginary
);

  wire not_1_out;

  not not_1 (not_1_out, Gnd_7);
  nor nor_1 (_1Y_3, _1A_1, _1B_2, _1B_2);
  nor nor_2 (_2Y_6, _2A_4, _2B_5, _2B_5);
  nor nor_3 (_3Y_10, _3A_8, _3B_9, _3B_9);
  nor nor_4 (_4Y_13, _4A_11, _4B_12, _4B_12);
  and and_1 (Power_Test_imaginary, Vcc_14, Vcc_14, not_1_out);

  // Notes on the sheet:
  //   _1B_2: pull=up
  //   _4B_12: pull=up
  //   _3B_9: pull=up
  //   _4A_11: pull=up
  //   _2A_4: pull=up
  //   _1A_1: pull=up
  //   _3A_8: pull=up
  //   _2B_5: pull=up
  //   Vcc_14: pull=down
  //   74xx00 Quad 2-input NOR Gate
  //   Copyright 2005 Technological Services Company
endmodule

module _74xx04 (
  input  _1A_1,
  input  _2A_3,
  input  _3A_5,
  input  _4A_9,
  input  _5A_11,
  input  _6A_13,
  input  Vcc_14,
  input  Gnd_7,
  output _1Y_2,
  output _2Y_4,
  output _3Y_6,
  output _4Y_8,
  output _5Y_10,
  output _6Y_12,
  output Power_Test_imaginary
);

  wire not_1_out;

  not not_1 (not_1_out, Gnd_7);
  not not_2 (_1Y_2, _1A_1);
  not not_3 (_2Y_4, _2A_3);
  not not_4 (_3Y_6, _3A_5);
  not not_5 (_4Y_8, _4A_9);
  not not_6 (_5Y_10, _5A_11);
  not not_7 (_6Y_12, _6A_13);
  and and_1 (Power_Test_imaginary, Vcc_14, Vcc_14, not_1_out);

  // Notes on the sheet:
  //   Vcc_14: pull=down
  //   _2A_3: pull=up
  //   _3A_5: pull=up
  //   _4A_9: pull=up
  //   _5A_11: pull=up
  //   _6A_13: pull=up
  //   _1A_1: pull=up
  //   74xx04 Hex Inverters
  //   Copyright 2005 Technological Services Company
endmodule

module _74xx08 (
  input  _1A_1,
  input  _1B_2,
  input  _2A_4,
  input  _2B_5,
  input  _3A_9,
  input  _3B_10,
  input  _4A_12,
  input  _4B_13,
  input  Vcc_14,
  input  Gnd_7,
  output _1Y_3,
  output _2Y_6,
  output _3Y_8,
  output _4Y_11,
  output Power_Test_imaginary
);

  wire not_1_out;

  not not_1 (not_1_out, Gnd_7);
  and and_1 (_1Y_3, _1A_1, _1B_2, _1B_2);
  and and_2 (_2Y_6, _2A_4, _2B_5, _2B_5);
  and and_3 (_3Y_8, _3A_9, _3B_10, _3B_10);
  and and_4 (_4Y_11, _4A_12, _4B_13, _4B_13);
  and and_5 (Power_Test_imaginary, Vcc_14, Vcc_14, not_1_out);

  // Notes on the sheet:
  //   _2A_4: pull=up
  //   Vcc_14: pull=down
  //   _1A_1: pull=up
  //   _3A_9: pull=up
  //   _4B_13: pull=up
  //   _3B_10: pull=up
  //   _1B_2: pull=up
  //   _4A_12: pull=up
  //   _2B_5: pull=up
  //   74xx08 Quad 2-input AND Gate
  //   Copyright 2005 Technological Services Company
endmodule

module _74xx10 (
  input  _1A_1,
  input  _1B_2,
  input  _1C_13,
  input  _2A_3,
  input  _2B_4,
  input  _2C_5,
  input  _3A_9,
  input  _3B_10,
  input  _3C_11,
  input  Vcc_14,
  input  Gnd_7,
  output _1Y_12,
  output _2Y_6,
  output _3Y_8,
  output Power_Test_imaginary
);

  wire not_1_out;

  not not_1 (not_1_out, Gnd_7);
  nand nand_1 (_1Y_12, _1A_1, _1B_2, _1C_13);
  nand nand_2 (_2Y_6, _2A_3, _2B_4, _2C_5);
  nand nand_3 (_3Y_8, _3A_9, _3B_10, _3C_11);
  and and_1 (Power_Test_imaginary, Vcc_14, Vcc_14, not_1_out);

  // Notes on the sheet:
  //   Vcc_14: pull=down
  //   _3B_10: pull=up
  //   _3A_9: pull=up
  //   _1C_13: pull=up
  //   _1A_1: pull=up
  //   _2B_4: pull=up
  //   _2C_5: pull=up
  //   _3C_11: pull=up
  //   _1B_2: pull=up
  //   _2A_3: pull=up
  //   74xx10 triple 3 input NAND Gate
  //   Copyright 2005 Technological Services Company
endmodule

module _74xx11 (
  input  _1A_1,
  input  _1B_2,
  input  _1C_13,
  input  _2A_3,
  input  _2B_4,
  input  _2C_5,
  input  _3A_9,
  input  _3B_10,
  input  _3C_11,
  input  Vcc_14,
  input  Gnd_7,
  output _1Y_12,
  output _2Y_6,
  output _3Y_8,
  output Power_Test_imaginary
);

  wire not_1_out;

  not not_1 (not_1_out, Gnd_7);
  and and_1 (_1Y_12, _1A_1, _1B_2, _1C_13);
  and and_2 (_2Y_6, _2A_3, _2B_4, _2C_5);
  and and_3 (_3Y_8, _3A_9, _3B_10, _3C_11);
  and and_4 (Power_Test_imaginary, Vcc_14, Vcc_14, not_1_out);

  // Notes on the sheet:
  //   _1B_2: pull=up
  //   _1C_13: pull=up
  //   _2C_5: pull=up
  //   _3C_11: pull=up
  //   _3B_10: pull=up
  //   _3A_9: pull=up
  //   Vcc_14: pull=down
  //   _2A_3: pull=up
  //   _1A_1: pull=up
  //   _2B_4: pull=up
  //   74xx11 triple 3 input AND Gate
  //   Copyright 2005 Technological Services Company
endmodule

module _74xx13 (
  input  _1A_1,
  input  _1B_2,
  input  _1C_4,
  input  _1D_5,
  input  _2A_9,
  input  _2B_10,
  input  _2C_12,
  input  _2D_13,
  input  Vcc_14,
  input  Gnd_7,
  output _1Y_6,
  output _2Y_8,
  output Power_Test_imaginary
);

  wire not_1_out;

  not not_1 (not_1_out, Gnd_7);
  nand nand_1 (_1Y_6, _1A_1, _1B_2, _1B_2, _1C_4, _1D_5);
  nand nand_2 (_2Y_8, _2A_9, _2B_10, _2B_10, _2C_12, _2D_13);
  and and_1 (Power_Test_imaginary, Vcc_14, Vcc_14, not_1_out);

  // Notes on the sheet:
  //   _1C_4: pull=up
  //   _2B_10: pull=up
  //   _1A_1: pull=up
  //   _2A_9: pull=up
  //   Vcc_14: pull=down
  //   _2C_12: pull=up
  //   _1B_2: pull=up
  //   74xx13 Dual  4  input NAND Gate
  //   Copyright 2005 Technological Services Company
endmodule

module _74xx14 (
  input  _1A_1,
  input  _2A_3,
  input  _3A_5,
  input  _4A_9,
  input  _5A_11,
  input  _6A_13,
  input  Vcc_14,
  input  Gnd_7,
  output _1Y_2,
  output _2Y_4,
  output _3Y_6,
  output _4Y_8,
  output _5Y_10,
  output _6Y_12,
  output Power_Test_imaginary
);

  wire not_1_out;

  not not_1 (not_1_out, Gnd_7);
  not not_2 (_1Y_2, _1A_1);
  not not_3 (_2Y_4, _2A_3);
  not not_4 (_3Y_6, _3A_5);
  not not_5 (_4Y_8, _4A_9);
  not not_6 (_5Y_10, _5A_11);
  not not_7 (_6Y_12, _6A_13);
  and and_1 (Power_Test_imaginary, Vcc_14, Vcc_14, not_1_out);

  // Notes on the sheet:
  //   _4A_9: pull=up
  //   _5A_11: pull=up
  //   _2A_3: pull=up
  //   _6A_13: pull=up
  //   Vcc_14: pull=down
  //   _1A_1: pull=up
  //   _3A_5: pull=up
  //   74xx14 Hex Inverters
  //   Copyright 2005 Technological Services Company
endmodule

module _74xx18 (
  input  _1A_1,
  input  _1B_2,
  input  _1C_4,
  input  _1D_5,
  input  _2A_9,
  input  _2B_10,
  input  _2C_12,
  input  _2D_13,
  input  Vcc_14,
  input  Gnd_7,
  output _1Y_6,
  output _2Y_8,
  output Power_Test_imaginary
);

  wire not_1_out;

  not not_1 (not_1_out, Gnd_7);
  nand nand_1 (_1Y_6, _1A_1, _1B_2, _1B_2, _1C_4, _1D_5);
  nand nand_2 (_2Y_8, _2A_9, _2B_10, _2B_10, _2C_12, _2D_13);
  and and_1 (Power_Test_imaginary, Vcc_14, Vcc_14, not_1_out);

  // Notes on the sheet:
  //   _2C_12: pull=up
  //   _1C_4: pull=up
  //   Vcc_14: pull=down
  //   _2B_10: pull=up
  //   _2A_9: pull=up
  //   _1B_2: pull=up
  //   _1A_1: pull=up
  //   74xx18  Dual  4-input NAND Gates
  //   Copyright 2005 Technological Services Company
  //   incomplete?
endmodule

module _74xx19 (
  input  _1A_1,
  input  _2A_3,
  input  _3A_5,
  input  _4A_9,
  input  _5A_11,
  input  _6A_13,
  input  Vcc_14,
  input  Gnd_7,
  output _1Y_2,
  output _2Y_4,
  output _3Y_6,
  output _4Y_8,
  output _5Y_10,
  output _6Y_12,
  output Power_Test_imaginary
);

  wire not_1_out;

  not not_1 (not_1_out, Gnd_7);
  not not_2 (_1Y_2, _1A_1);
  not not_3 (_2Y_4, _2A_3);
  not not_4 (_3Y_6, _3A_5);
  not not_5 (_4Y_8, _4A_9);
  not not_6 (_5Y_10, _5A_11);
  not not_7 (_6Y_12, _6A_13);
  and and_1 (Power_Test_imaginary, Vcc_14, Vcc_14, not_1_out);

  // Notes on the sheet:
  //   _6A_13: pull=up
  //   _1A_1: pull=up
  //   _5A_11: pull=up
  //   _3A_5: pull=up
  //   Vcc_14: pull=down
  //   _4A_9: pull=up
  //   _2A_3: pull=up
  //   74xx19 Hex Inverters
  //   Copyright 2005 Technological Services Company
endmodule

module _74xx20 (
  input  _1A_1,
  input  _1B_2,
  input  _1C_4,
  input  _1D_5,
  input  _2A_9,
  input  _2B_10,
  input  _2C_12,
  input  _2D_13,
  input  Vcc_14,
  input  Gnd_7,
  output _1Y_6,
  output _2Y_8,
  output Power_Test_imaginary
);

  wire not_1_out;

  not not_1 (not_1_out, Gnd_7);
  nand nand_1 (_1Y_6, _1A_1, _1B_2, _1B_2, _1C_4, _1D_5);
  nand nand_2 (_2Y_8, _2A_9, _2B_10, _2B_10, _2C_12, _2D_13);
  and and_1 (Power_Test_imaginary, Vcc_14, Vcc_14, not_1_out);

  // Notes on the sheet:
  //   _2C_12: pull=up
  //   _1A_1: pull=up
  //   _2A_9: pull=up
  //   Vcc_14: pull=down
  //   _1B_2: pull=up
  //   _2B_10: pull=up
  //   _1C_4: pull=up
  //   74xx20  Dual  4  input NAND Gate
  //   Copyright 2005 Technological Services Company
endmodule

module _74xx21 (
  input  _1A_1,
  input  _1B_2,
  input  _1C_4,
  input  _1D_5,
  input  _2A_9,
  input  _2B_10,
  input  _2C_12,
  input  _2D_13,
  input  Vcc_14,
  input  Gnd_7,
  output _1Y_6,
  output _2Y_8,
  output Power_Test_imaginary
);

  wire not_1_out;

  not not_1 (not_1_out, Gnd_7);
  and and_1 (_1Y_6, _1A_1, _1B_2, _1B_2, _1C_4, _1D_5);
  and and_2 (_2Y_8, _2A_9, _2B_10, _2B_10, _2C_12, _2D_13);
  and and_3 (Power_Test_imaginary, Vcc_14, Vcc_14, not_1_out);

  // Notes on the sheet:
  //   _2C_12: pull=up
  //   _2A_9: pull=up
  //   _2B_10: pull=up
  //   _1C_4: pull=up
  //   Vcc_14: pull=down
  //   _1B_2: pull=up
  //   _1A_1: pull=up
  //   74xx21  Dual  4  input AND Gate
  //   Copyright 2005 Technological Services Company
endmodule

module _74xx24 (
  input  _1A_1,
  input  _1B_2,
  input  _2A_4,
  input  _2B_5,
  input  _3A_9,
  input  _3B_10,
  input  _4A_12,
  input  _4B_13,
  input  Vcc_14,
  input  Gnd_7,
  output _1Y_3,
  output _2Y_6,
  output _3Y_8,
  output _4Y_11,
  output Power_Test_imaginary
);

  wire not_1_out;

  not not_1 (not_1_out, Gnd_7);
  nand nand_1 (_1Y_3, _1A_1, _1B_2, _1B_2);
  nand nand_2 (_2Y_6, _2A_4, _2B_5, _2B_5);
  nand nand_3 (_3Y_8, _3A_9, _3B_10, _3B_10);
  nand nand_4 (_4Y_11, _4A_12, _4B_13, _4B_13);
  and and_1 (Power_Test_imaginary, Vcc_14, Vcc_14, not_1_out);

  // Notes on the sheet:
  //   _3A_9: pull=up
  //   _4A_12: pull=up
  //   _3B_10: pull=up
  //   _2A_4: pull=up
  //   _1A_1: pull=up
  //   _4B_13: pull=up
  //   Vcc_14: pull=down
  //   _1B_2: pull=up
  //   _2B_5: pull=up
  //   74xx24 Quad 2-input NAND Gate
  //   Copyright 2005 Technological Services Company
endmodule

module _74xx25 (
  input  _1A_1,
  input  _1B_2,
  input  _1C__4,
  input  _1D__5,
  input  _1G__3,
  input  _2A_9,
  input  _2B_10,
  input  _2C__12,
  input  _2D__13,
  input  _2G__11,
  input  Vcc_14,
  input  Gnd_7,
  output _1Y_3,
  output _2Y_8,
  output Power_Test_imaginary
);

  wire not_1_out, or_1_out, or_2_out;

  not not_1 (not_1_out, Gnd_7);
  or or_1 (or_1_out, _1A_1, _1B_2, _1B_2, _1C__4, _1D__5);
  or or_2 (or_2_out, _2A_9, _2B_10, _2B_10, _2C__12, _2D__13);
  nand nand_1 (_1Y_3, or_1_out, _1G__3, _1G__3);
  nand nand_2 (_2Y_8, or_2_out, _2G__11, _2G__11);
  and and_1 (Power_Test_imaginary, Vcc_14, Vcc_14, not_1_out);

  // Notes on the sheet:
  //   _1A_1: pull=up
  //   _1B_2: pull=up
  //   _2A_9: pull=up
  //   Vcc_14: pull=down
  //   _2B_10: pull=up
  //   74xx25 Quad 2-input NOR Gate
  //   Copyright 2005 Technological Services Company
endmodule

module _74xx27 (
  input  _1A_1,
  input  _1B_2,
  input  _1C_13,
  input  _2A_3,
  input  _2B_4,
  input  _2C_5,
  input  _3A_9,
  input  _3B_10,
  input  _3C_11,
  input  Vcc_14,
  input  Gnd_7,
  output _1Y_12,
  output _2Y_6,
  output _3Y_8,
  output Power_Test_imaginary
);

  wire not_1_out;

  not not_1 (not_1_out, Gnd_7);
  nor nor_1 (_1Y_12, _1A_1, _1B_2, _1C_13);
  nor nor_2 (_2Y_6, _2A_3, _2B_4, _2C_5);
  nor nor_3 (_3Y_8, _3A_9, _3B_10, _3C_11);
  and and_1 (Power_Test_imaginary, Vcc_14, Vcc_14, not_1_out);

  // Notes on the sheet:
  //   _1B_2: pull=up
  //   Vcc_14: pull=down
  //   _2B_4: pull=up
  //   _3B_10: pull=up
  //   _2A_3: pull=up
  //   _3C_11: pull=up
  //   _2C_5: pull=up
  //   _1A_1: pull=up
  //   _3A_9: pull=up
  //   _1C_13: pull=up
  //   74xx27 triple 3 input NOR Gate
  //   Copyright 2005 Technological Services Company
endmodule

module _74xx28 (
  input  _1A_2,
  input  _1B_3,
  input  _2A_5,
  input  _2B_6,
  input  _3A_9,
  input  _3B_9,
  input  _4A_11,
  input  _4B_12,
  input  Vcc_14,
  input  Gnd_7,
  output _1Y_1,
  output _2Y_4,
  output _3Y_10,
  output _4Y_13,
  output Power_Test_imaginary
);

  wire not_1_out;

  not not_1 (not_1_out, Gnd_7);
  nor nor_1 (_1Y_1, _1A_2, _1B_3, _1B_3);
  nor nor_2 (_2Y_4, _2A_5, _2B_6, _2B_6);
  nor nor_3 (_3Y_10, _3A_9, _3B_9, _3B_9);
  nor nor_4 (_4Y_13, _4A_11, _4B_12, _4B_12);
  and and_1 (Power_Test_imaginary, Vcc_14, Vcc_14, not_1_out);

  // Notes on the sheet:
  //   _2A_5: pull=up
  //   _4B_12: pull=up
  //   _3B_9: pull=up
  //   _4A_11: pull=up
  //   _1B_3: pull=up
  //   _2B_6: pull=up
  //   _1A_2: pull=up
  //   Vcc_14: pull=down
  //   _3A_9: pull=up
  //   74xx28 Quad 2-input NOR Gate
  //   Copyright 2005 Technological Services Company
endmodule

module _74xx30 (
  input  A_1,
  input  B_2,
  input  C_3,
  input  D_4,
  input  E_5,
  input  F_6,
  input  G_11,
  input  H_12,
  input  Vcc_14,
  input  Gnd_7,
  output nY_8,
  output Power_Test_imaginary
);

  wire not_1_out;

  not not_1 (not_1_out, Gnd_7);
  nand nand_1 (nY_8, A_1, B_2, C_3, D_4, E_5, E_5, F_6, G_11, H_12);
  and and_1 (Power_Test_imaginary, Vcc_14, Vcc_14, not_1_out);

  // Notes on the sheet:
  //   Vcc_14: pull=down
  //   74xx30 8-input NAND Gate
  //   Copyright 2005 Technological Services Company
endmodule

module _74xx32 (
  input  _1A_1,
  input  _1B_2,
  input  _2A_4,
  input  _2B_5,
  input  _3A_9,
  input  _3B_10,
  input  _4A_12,
  input  _4B_13,
  input  Vcc_14,
  input  Gnd_7,
  output _1Y_3,
  output _2Y_6,
  output _3Y_8,
  output _4Y_11,
  output Power_Test_imaginary
);

  wire not_1_out;

  not not_1 (not_1_out, Gnd_7);
  or or_1 (_1Y_3, _1A_1, _1B_2, _1B_2);
  or or_2 (_2Y_6, _2A_4, _2B_5, _2B_5);
  or or_3 (_3Y_8, _3A_9, _3B_10, _3B_10);
  or or_4 (_4Y_11, _4A_12, _4B_13, _4B_13);
  and and_1 (Power_Test_imaginary, Vcc_14, Vcc_14, not_1_out);

  // Notes on the sheet:
  //   _2B_5: pull=up
  //   _3B_10: pull=up
  //   _2A_4: pull=up
  //   _4A_12: pull=up
  //   _3A_9: pull=up
  //   _4B_13: pull=up
  //   _1A_1: pull=up
  //   _1B_2: pull=up
  //   Vcc_14: pull=down
  //   74xx32 Quad 2-input OR Gate
  //   Copyright 2005 Technological Services Company
endmodule

module _74xx37 (
  input  _1A_1,
  input  _1B_2,
  input  _2A_4,
  input  _2B_5,
  input  _3A_9,
  input  _3B_10,
  input  _4A_12,
  input  _4B_13,
  input  Vcc_14,
  input  Gnd_7,
  output _1Y_3,
  output _2Y_6,
  output _3Y_8,
  output _4Y_11,
  output Power_Test_imaginary
);

  wire not_1_out;

  not not_1 (not_1_out, Gnd_7);
  nand nand_1 (_1Y_3, _1A_1, _1B_2, _1B_2);
  nand nand_2 (_2Y_6, _2A_4, _2B_5, _2B_5);
  nand nand_3 (_3Y_8, _3A_9, _3B_10, _3B_10);
  nand nand_4 (_4Y_11, _4A_12, _4B_13, _4B_13);
  and and_1 (Power_Test_imaginary, Vcc_14, Vcc_14, not_1_out);

  // Notes on the sheet:
  //   _4A_12: pull=up
  //   Vcc_14: pull=down
  //   _3A_9: pull=up
  //   _1A_1: pull=up
  //   _3B_10: pull=up
  //   _4B_13: pull=up
  //   _1B_2: pull=up
  //   _2A_4: pull=up
  //   _2B_5: pull=up
  //   74xx37 Quad 2-input NAND Gate
  //   Copyright 2005 Technological Services Company
endmodule

module _74xx40 (
  input  _1A_1,
  input  _1B_2,
  input  _1C_4,
  input  _1D_5,
  input  _2A_9,
  input  _2B_10,
  input  _2C_12,
  input  _2D_13,
  input  Vcc_14,
  input  Gnd_7,
  output _1Y_6,
  output _2Y_8,
  output Power_Test_imaginary
);

  wire not_1_out;

  not not_1 (not_1_out, Gnd_7);
  nand nand_1 (_1Y_6, _1A_1, _1B_2, _1B_2, _1C_4, _1D_5);
  nand nand_2 (_2Y_8, _2A_9, _2B_10, _2B_10, _2C_12, _2D_13);
  and and_1 (Power_Test_imaginary, Vcc_14, Vcc_14, not_1_out);

  // Notes on the sheet:
  //   Vcc_14: pull=down
  //   _2A_9: pull=up
  //   _1A_1: pull=up
  //   _1C_4: pull=up
  //   _1B_2: pull=up
  //   _2C_12: pull=up
  //   _2B_10: pull=up
  //   74xx240  Dual  4-input NAND Gates
  //   Copyright 2005 Technological Services Company
endmodule

module _74xx42 (
  input  S0_15,
  input  S1_14,
  input  S2_13,
  input  S3_12,
  input  Vcc_14,
  input  Gnd_7,
  output Y0_1,
  output Y1_2,
  output Y2_3,
  output Y3_4,
  output Y4_5,
  output Y5_6,
  output Y6_7,
  output Y7_9,
  output Y8_10,
  output Y9_11,
  output Power_Test_imaginary
);

  wire not_1_out, not_2_out, not_3_out, not_4_out, not_5_out;

  not not_1 (not_1_out, S0_15);
  not not_2 (not_2_out, S1_14);
  not not_3 (not_3_out, S2_13);
  not not_4 (not_4_out, S3_12);
  not not_5 (not_5_out, Gnd_7);
  nand nand_1 (Y0_1, not_1_out, not_2_out, not_3_out, not_4_out, not_4_out);
  nand nand_2 (Y1_2, S0_15, not_2_out, not_3_out, not_4_out, not_4_out);
  nand nand_3 (Y2_3, not_1_out, S1_14, not_3_out, not_4_out, not_4_out);
  nand nand_4 (Y3_4, S0_15, S1_14, not_3_out, not_4_out, not_4_out);
  nand nand_5 (Y4_5, not_1_out, not_2_out, S2_13, not_4_out, not_4_out);
  nand nand_6 (Y5_6, S0_15, not_2_out, S2_13, not_4_out, not_4_out);
  nand nand_7 (Y6_7, not_1_out, S1_14, S2_13, not_4_out, not_4_out);
  nand nand_8 (Y7_9, S0_15, S1_14, S2_13, not_4_out, not_4_out);
  nand nand_9 (Y8_10, not_1_out, not_2_out, not_3_out, S3_12, S3_12);
  nand nand_10 (Y9_11, S0_15, not_2_out, not_3_out, S3_12, S3_12);
  and and_1 (Power_Test_imaginary, Vcc_14, Vcc_14, not_5_out);

  // Notes on the sheet:
  //   Vcc_14: pull=down
  //   74xx42 1-of-10 Inverting Decoder/Demultiplexer
  //   Copyright 2005 Technological Services Company
endmodule

module _74xx55 (
  input  A__1,
  input  B__2,
  input  C__3,
  input  D__4,
  input  H__13,
  input  G__12,
  input  F__11,
  input  E__10,
  input  Vcc_14,
  input  Gnd_7,
  output Y__8,
  output Power_Test_imaginary
);

  wire and_1_out, and_2_out, not_1_out;

  not not_1 (not_1_out, Gnd_7);
  and and_1 (and_1_out, A__1, B__2, C__3, D__4, D__4);
  and and_2 (and_2_out, H__13, G__12, F__11, E__10, E__10);
  and and_3 (Power_Test_imaginary, Vcc_14, Vcc_14, not_1_out);
  nor nor_1 (Y__8, and_1_out, and_2_out, and_2_out);

  // Notes on the sheet:
  //   Vcc_14: pull=down
  //   74xx55 2-Wide 4-Input AND-NOR Gate
  //   Copyright 2005 Technological Services Company
endmodule

module _74xx260 (
  input  _1A__1,
  input  _1B__2,
  input  _1C__4,
  input  _1D__5,
  input  _1E__3,
  input  _2A__9,
  input  _2B__10,
  input  _2C__12,
  input  _2D__13,
  input  _2E__11,
  input  Vcc_14,
  input  Gnd_7,
  output _1Y__6,
  output _2Y__8,
  output Power_Test_imaginary
);

  wire not_1_out;

  not not_1 (not_1_out, Gnd_7);
  nor nor_1 (_1Y__6, _1A__1, _1B__2, _1C__4, _1D__5, _1E__3);
  nor nor_2 (_2Y__8, _2A__9, _2B__10, _2C__12, _2D__13, _2E__11);
  and and_1 (Power_Test_imaginary, Vcc_14, Vcc_14, not_1_out);

  // Notes on the sheet:
  //   Vcc_14: pull=down
  //   74260 Dual 5-Input NOR Gates
  //   Copyright 2005 Technological Services Company
endmodule

module _74xx590 (
  input  CPR_13,
  input  CPC_11,
  input  nCE_12,
  input  nMRC_10,
  input  nOE_14,
  output Q0_15,
  output Q1_1,
  output Q2_2,
  output Q3_3,
  output Q4_4,
  output Q5_5,
  output Q6_6,
  output Q7_7,
  output nRCO_9
);

  wire and_1_out, j_k_ff_1_qn, j_k_ff_2_qn, j_k_ff_3_qn, j_k_ff_4_qn, j_k_ff_5_qn, j_k_ff_6_qn, j_k_ff_7_qn,
       not_1_out, not_2_out, not_3_out;
  wire [7:0] j_k_ff_1_q, register_1_q;

  J_K_Flip_Flop j_k_ff_1 (
    .J(not_1_out), .clk(CPC_11), .K(not_1_out), .Q(j_k_ff_1_q[0]), .Qn(j_k_ff_1_qn), .preset(1'b0),
    .reset(not_2_out));  // open: en
  not not_1 (not_1_out, nCE_12);
  not not_2 (not_2_out, nMRC_10);
  not not_3 (not_3_out, nOE_14);
  J_K_Flip_Flop j_k_ff_2 (
    .J(not_1_out), .clk(j_k_ff_1_qn), .K(not_1_out), .Q(j_k_ff_1_q[1]), .Qn(j_k_ff_2_qn), .preset(1'b0),
    .reset(not_2_out));  // open: en
  J_K_Flip_Flop j_k_ff_3 (
    .J(not_1_out), .clk(j_k_ff_2_qn), .K(not_1_out), .Q(j_k_ff_1_q[2]), .Qn(j_k_ff_3_qn), .preset(1'b0),
    .reset(not_2_out));  // open: en
  J_K_Flip_Flop j_k_ff_4 (
    .J(not_1_out), .clk(j_k_ff_3_qn), .K(not_1_out), .Q(j_k_ff_1_q[3]), .Qn(j_k_ff_4_qn), .preset(1'b0),
    .reset(not_2_out));  // open: en
  J_K_Flip_Flop j_k_ff_5 (
    .J(not_1_out), .clk(j_k_ff_4_qn), .K(not_1_out), .Q(j_k_ff_1_q[4]), .Qn(j_k_ff_5_qn), .preset(1'b0),
    .reset(not_2_out));  // open: en
  J_K_Flip_Flop j_k_ff_6 (
    .J(not_1_out), .clk(j_k_ff_5_qn), .K(not_1_out), .Q(j_k_ff_1_q[5]), .Qn(j_k_ff_6_qn), .preset(1'b0),
    .reset(not_2_out));  // open: en
  J_K_Flip_Flop j_k_ff_7 (
    .J(not_1_out), .clk(j_k_ff_6_qn), .K(not_1_out), .Q(j_k_ff_1_q[6]), .Qn(j_k_ff_7_qn), .preset(1'b0),
    .reset(not_2_out));  // open: en
  and and_1 (and_1_out, j_k_ff_1_q[0], j_k_ff_1_q[1], j_k_ff_1_q[2], j_k_ff_1_q[3], j_k_ff_1_q[4], j_k_ff_1_q[5], j_k_ff_1_q[6], j_k_ff_1_q[7], j_k_ff_1_q[7]);
  J_K_Flip_Flop j_k_ff_8 (
    .J(not_1_out), .clk(j_k_ff_7_qn), .K(not_1_out), .Q(j_k_ff_1_q[7]), .preset(1'b0), .reset(not_2_out));  // open: Qn, en
  Register #(.width(8)) register_1 (.D(j_k_ff_1_q), .Q(register_1_q), .clk(CPR_13), .clr(not_2_out));  // open: en
  assign {Q7_7, Q6_6, Q5_5, Q4_4, Q3_3, Q2_2, Q1_1, Q0_15} = not_3_out ? register_1_q : 8'bz;  // Controlled_Buffer controlled_buffer_1
  not not_4 (nRCO_9, and_1_out);

  // Notes on the sheet:
  //   nOE_14: pull=up
  //   74xx590 8 bit counter
  //   Copyright 2005 Technological Services Company
endmodule
